// Logisim project #1.circ as structural Verilog: 1 circuit, main circuit main
module main (
  input  x,
  input  y,
  input  z
);

  wire and_1_out, and_2_out, or_1_out, or_2_out, x_prime_out, xnor_1_out, xor_1_out, xy_out, xz_out, yz_out,
       z_prime_out;

  not x_prime (x_prime_out, x);
  not z_prime (z_prime_out, z);
  // NOT_Gate y_prime has open pins: in=y, out=open
  and xy (xy_out, x, y);
  and xz (xz_out, x, z);
  and yz (yz_out, y, z);
  xnor xnor_1 (xnor_1_out, y, z);
  xor xor_1 (xor_1_out, y, z);
  or or_1 (or_1_out, xy_out, xz_out, yz_out);
  and and_1 (and_1_out, x, xnor_1_out);
  and and_2 (and_2_out, xor_1_out, x_prime_out);
  LED a (.in(or_1_out));
  LED b (.in(or_2_out));
  or or_2 (or_2_out, and_1_out, and_2_out);
  LED c (.in(z_prime_out));

  // Notes on the sheet:
  //   z'
  //   x(y XNOR z)
  //   x'(y XOR z)
endmodule
