// Logisim project #2.circ as structural Verilog: 1 circuit, main circuit main
module main (
  input  a,
  input  b,
  input  c,
  input  d
);

  wire a_prime_b_out, a_prime_c_out, a_prime_d_out, a_prime_out, ab_prime_c_prime_d_prime_out, b_prime_c_out,
       b_prime_d_out, b_prime_out, bc_prime_d_prime_out, c_prime_out, d_prime_out, or_1_out, or_2_out,
       xor_1_out;

  not a_prime (a_prime_out, a);
  not c_prime (c_prime_out, c);
  not b_prime (b_prime_out, b);
  not d_prime (d_prime_out, d);
  and a_prime_b (a_prime_b_out, a_prime_out, b);
  and a_prime_d (a_prime_d_out, a_prime_out, d);
  and a_prime_c (a_prime_c_out, a_prime_out, c);
  and ab_prime_c_prime_d_prime (ab_prime_c_prime_d_prime_out, a, b_prime_out, c_prime_out, d_prime_out);
  and b_prime_d (b_prime_d_out, b_prime_out, d);
  and b_prime_c (b_prime_c_out, b_prime_out, c);
  and bc_prime_d_prime (bc_prime_d_prime_out, b, c_prime_out, d_prime_out);
  xor xor_1 (xor_1_out, c, d);
  LED x (.in(or_2_out));
  LED w (.in(or_1_out));
  or or_1 (or_1_out, a_prime_b_out, a_prime_d_out, a_prime_c_out, ab_prime_c_prime_d_prime_out);
  or or_2 (or_2_out, b_prime_d_out, b_prime_c_out, bc_prime_d_prime_out);
  LED z (.in(d));
  LED y (.in(xor_1_out));

  // Notes on the sheet:
  //   c XOR d
  //   d
endmodule
