// Logisim project #4.circ as structural Verilog: 1 circuit, main circuit main
module main (
  input  X,
  input  Y
);

  wire clock_1_out, Da_q, Da_qn, Db_q, Db_qn, or_1_out, or_2_out, X_prime_B_out, X_prime_out, X_prime_Y_out,
       XA_2_out, XA_out;

  not X_prime (X_prime_out, X);
  // NOT_Gate Y_prime has open pins: in=Y, out=open
  and X_prime_Y (X_prime_Y_out, X_prime_out, Y);
  and XA (XA_out, X, Da_q);
  and X_prime_B (X_prime_B_out, X_prime_out, Db_q);
  and XA_2 (XA_2_out, X, Da_q);
  or or_1 (or_1_out, X_prime_Y_out, XA_out);
  or or_2 (or_2_out, X_prime_B_out, XA_2_out);
  Clock clock_1 (.out(clock_1_out));
  LED led_1 (.in(Da_q));
  D_Flip_Flop Da (.clk(clock_1_out), .D(or_1_out), .Q(Da_q), .Qn(Da_qn));  // open: preset, en, reset
  D_Flip_Flop Db (.clk(clock_1_out), .D(or_2_out), .Q(Db_q), .Qn(Db_qn));  // open: preset, en, reset
  LED Z (.in(Db_q));
  LED led_2 (.in(Db_q));

  // Notes on the sheet:
  //   Clock
  //   A(t+1)
  //   A
  //   A'
  //   B
  //   B'
  //   B(t+1)
endmodule
