// Logisim project Bank Lab.circ as structural Verilog: 1 circuit, main circuit main
module main (
  input  F,
  input  H,
  input  P,
  input  S,
  input  T
);

  wire and_1_out, and_2_out, and_3_out, and_4_out, and_5_out, or_1_out;

  and and_1 (and_1_out, H, P, T);
  and and_2 (and_2_out, H, S, T);
  and and_3 (and_3_out, F, H, P);
  and and_4 (and_4_out, F, S, T);
  and and_5 (and_5_out, F, P, S);
  or or_1 (or_1_out, and_1_out, and_2_out, and_3_out, and_4_out, and_5_out);
  LED Q (.in(or_1_out));
endmodule
