// Logisim project Lab 11a.circ as structural Verilog: 1 circuit, main circuit main
module main (
  input  A3,
  input  A2,
  input  A1,
  input  A0,
  input  B3,
  input  B2,
  input  B1,
  input  B0
);

  wire and_1_out, and_2_out, and_3_out, and_4_out, and_5_out, and_6_out, and_7_out, and_8_out, and_9_out,
       C0_out, C1_out, C2_out, C3_2_out, xor_1_out, xor_2_out, xor_3_out, xor_4_out, xor_5_out, xor_6_out,
       xor_7_out;

  xor xor_1 (xor_1_out, A0, B0);
  and C0 (C0_out, A0, B0);
  and and_1 (and_1_out, A1, B1);
  and and_2 (and_2_out, C0_out, A1);
  and and_3 (and_3_out, C0_out, B1);
  xor xor_2 (xor_2_out, A1, B1);
  and and_4 (and_4_out, A2, B2);
  and and_5 (and_5_out, C1_out, A2);
  and and_6 (and_6_out, C1_out, B2);
  xor xor_3 (xor_3_out, A2, B2);
  and and_7 (and_7_out, A3, B3);
  and and_8 (and_8_out, C2_out, A3);
  and and_9 (and_9_out, C2_out, B3);
  xor xor_4 (xor_4_out, A3, B3);
  LED S3 (.in(xor_7_out));
  LED C3 (.in(C3_2_out));
  or C1 (C1_out, and_1_out, and_2_out, and_3_out);
  xor xor_5 (xor_5_out, xor_2_out, C0_out);
  or C2 (C2_out, and_4_out, and_5_out, and_6_out);
  xor xor_6 (xor_6_out, xor_3_out, C1_out);
  or C3_2 (C3_2_out, and_7_out, and_8_out, and_9_out);
  xor xor_7 (xor_7_out, xor_4_out, C2_out);
  LED S1 (.in(xor_5_out));
  LED S2 (.in(xor_6_out));
  LED S0 (.in(xor_1_out));
endmodule
