// Logisim project Lab 11b.circ as structural Verilog: 1 circuit, main circuit main
module main (
  input  A,
  input  B,
  input  C,
  input  D
);

  wire a_out, A_prime_B_out, A_prime_B_prime_C_2_out, A_prime_B_prime_C_out, A_prime_B_prime_out,
       A_prime_BC_prime_2_out, A_prime_BC_prime_D_out, A_prime_BC_prime_out, A_prime_BCD_prime_out,
       A_prime_BD_out, A_prime_C_out, A_prime_C_prime_D_prime_2_out, A_prime_C_prime_D_prime_out,
       A_prime_C_prime_out, A_prime_CD_2_out, A_prime_CD_out, A_prime_CD_prime_2_out, A_prime_CD_prime_3_out,
       A_prime_CD_prime_out, A_prime_out, AB_prime_C_prime_2_out, AB_prime_C_prime_3_out,
       AB_prime_C_prime_4_out, AB_prime_C_prime_out, b_out, B_prime_C_prime_2_out,
       B_prime_C_prime_D_prime_2_out, B_prime_C_prime_D_prime_3_out, B_prime_C_prime_D_prime_out,
       B_prime_C_prime_out, B_prime_out, c_out, C_prime_out, d_out, D_prime_out, e_out, f_out, g_out;

  not A_prime (A_prime_out, A);
  not B_prime (B_prime_out, B);
  not C_prime (C_prime_out, C);
  not D_prime (D_prime_out, D);
  and A_prime_C (A_prime_C_out, A_prime_out, C);
  and AB_prime_C_prime (AB_prime_C_prime_out, A, B_prime_out, C_prime_out);
  and A_prime_BD (A_prime_BD_out, A_prime_out, B, D);
  and B_prime_C_prime_D_prime (B_prime_C_prime_D_prime_out, B_prime_out, C_prime_out, D_prime_out);
  and A_prime_B_prime (A_prime_B_prime_out, A_prime_out, B_prime_out);
  and B_prime_C_prime (B_prime_C_prime_out, B_prime_out, C_prime_out);
  and A_prime_CD (A_prime_CD_out, A_prime_out, C, D);
  and A_prime_C_prime_D_prime (A_prime_C_prime_D_prime_out, A_prime_out, C_prime_out, D_prime_out);
  and A_prime_C_prime (A_prime_C_prime_out, A_prime_out, C_prime_out);
  and A_prime_B (A_prime_B_out, A_prime_out, B);
  and B_prime_C_prime_2 (B_prime_C_prime_2_out, B_prime_out, C_prime_out);
  and A_prime_CD_2 (A_prime_CD_2_out, A_prime_out, C, D);
  and AB_prime_C_prime_2 (AB_prime_C_prime_2_out, A, B_prime_out, C_prime_out);
  and A_prime_B_prime_C (A_prime_B_prime_C_out, A_prime_out, B_prime_out, C);
  and A_prime_CD_prime (A_prime_CD_prime_out, B, C, D_prime_out);
  and B_prime_C_prime_D_prime_2 (B_prime_C_prime_D_prime_2_out, B_prime_out, C_prime_out, D_prime_out);
  and A_prime_BC_prime_D (A_prime_BC_prime_D_out, A_prime_out, B, C_prime_out, D);
  or u_a (a_out, A_prime_C_out, AB_prime_C_prime_out, A_prime_BD_out, B_prime_C_prime_D_prime_out);
  or u_b (b_out, A_prime_B_prime_out, B_prime_C_prime_out, A_prime_CD_out, A_prime_C_prime_D_prime_out);
  or u_c (c_out, A_prime_C_prime_out, A_prime_B_out, B_prime_C_prime_2_out, A_prime_CD_2_out);
  or u_d (d_out, AB_prime_C_prime_2_out, A_prime_B_prime_C_out, A_prime_CD_prime_out, B_prime_C_prime_D_prime_2_out, A_prime_BC_prime_D_out);
  _7_Segment_Display u_7_segment_display_1 (
    .g(g_out), .f(f_out), .a(a_out), .b(b_out), .e(e_out), .d(d_out), .c(c_out));  // open: dp
  or e (e_out, A_prime_CD_prime_2_out, B_prime_C_prime_D_prime_3_out);
  and A_prime_CD_prime_2 (A_prime_CD_prime_2_out, A_prime_out, C, D_prime_out);
  and B_prime_C_prime_D_prime_3 (B_prime_C_prime_D_prime_3_out, B_prime_out, C_prime_out, D_prime_out);
  and A_prime_BCD_prime (A_prime_BCD_prime_out, A_prime_out, B, C, D_prime_out);
  and A_prime_BC_prime (A_prime_BC_prime_out, A_prime_out, B, C_prime_out);
  or f (f_out, A_prime_BC_prime_out, A_prime_BCD_prime_out, AB_prime_C_prime_3_out, A_prime_C_prime_D_prime_2_out);
  and AB_prime_C_prime_3 (AB_prime_C_prime_3_out, A, B_prime_out, C_prime_out);
  and A_prime_C_prime_D_prime_2 (A_prime_C_prime_D_prime_2_out, A_prime_out, C_prime_out, D_prime_out);
  and AB_prime_C_prime_4 (AB_prime_C_prime_4_out, A, B_prime_out, C_prime_out);
  or g (g_out, AB_prime_C_prime_4_out, A_prime_BC_prime_2_out, A_prime_CD_prime_3_out, A_prime_B_prime_C_2_out);
  and A_prime_CD_prime_3 (A_prime_CD_prime_3_out, A_prime_out, C, D_prime_out);
  and A_prime_BC_prime_2 (A_prime_BC_prime_2_out, A_prime_out, B, C_prime_out);
  and A_prime_B_prime_C_2 (A_prime_B_prime_C_2_out, A_prime_out, B_prime_out, C);
endmodule
