// Logisim project Lab 12a.circ as structural Verilog: 1 circuit, main circuit main
module main (
  input  A0,
  input  A1,
  input  B0,
  input  B1
);

  wire A_prime_0_out, A_prime_1_out, and_1_out, and_2_out, and_3_out, and_4_out, and_5_out, and_6_out,
       and_7_out, B_prime_0_out, B_prime_1_out, or_1_out, or_2_out, xnor_1_out, xnor_2_out;

  not A_prime_0 (A_prime_0_out, A0);
  not A_prime_1 (A_prime_1_out, A1);
  not B_prime_0 (B_prime_0_out, B0);
  not B_prime_1 (B_prime_1_out, B1);
  xnor xnor_1 (xnor_1_out, A_prime_1_out, B_prime_1_out);
  xnor xnor_2 (xnor_2_out, A0, B0);
  and and_1 (and_1_out, A_prime_0_out, B0);
  and and_2 (and_2_out, A1, B0, B_prime_1_out);
  and and_3 (and_3_out, A_prime_0_out, A1, B_prime_1_out);
  and and_4 (and_4_out, A0, B_prime_0_out);
  and and_5 (and_5_out, A0, A_prime_1_out, B1);
  and and_6 (and_6_out, A1, B_prime_0_out, B1);
  or or_1 (or_1_out, and_1_out, and_2_out, and_3_out);
  or or_2 (or_2_out, and_4_out, and_5_out, and_6_out);
  LED E (.in(and_7_out));
  and and_7 (and_7_out, xnor_1_out, xnor_2_out);
  LED G (.in(or_1_out));
  LED L (.in(or_2_out));
endmodule
