// Logisim project Lab 12b.circ as structural Verilog: 1 circuit, main circuit main
module main (
  input  L,
  input  M0,
  input  M1,
  input  M2,
  input  M3
);

  wire and_1_out, and_2_out, and_3_out, and_4_out, and_5_out, and_6_out, and_7_out, L_prime_out,
       M0_prime_out, M1_prime_out, M2_prime_out, M3_prime_out, or_1_out, xor_1_out;

  not L_prime (L_prime_out, L);
  not M0_prime (M0_prime_out, M0);
  not M1_prime (M1_prime_out, M1);
  not M2_prime (M2_prime_out, M2);
  not M3_prime (M3_prime_out, M3);
  and and_1 (and_1_out, M0_prime_out, M1_prime_out, M2, M3_prime_out, L_prime_out);
  and and_2 (and_2_out, M0_prime_out, M1_prime_out, M2, M3_prime_out, L);
  and and_3 (and_3_out, M0, M1_prime_out, M3);
  and and_4 (and_4_out, M0_prime_out, M1, M3_prime_out);
  and and_5 (and_5_out, M0_prime_out, M3);
  and and_6 (and_6_out, M0, M2_prime_out, M3_prime_out);
  and and_7 (and_7_out, M0, M1_prime_out, M3_prime_out);
  xor xor_1 (xor_1_out, and_3_out, and_4_out);
  or or_1 (or_1_out, and_5_out, and_6_out, and_7_out);
  LED _28 (.in(and_1_out));
  LED _29 (.in(and_2_out));
  LED _30 (.in(xor_1_out));
  LED _31 (.in(or_1_out));
endmodule
