// Logisim project Lab 13a.circ as structural Verilog: 1 circuit, main circuit main
module main (
);

  wire A_prime_B_out, A_prime_B_prime_C_prime_2_out, A_prime_B_prime_C_prime_out, A_prime_BC_out,
       BC_prime_out, clock_1_out, Da_q, Da_qn, Db_q, Db_qn, Dc_q, Dc_qn, or_1_out, or_2_out;

  and A_prime_B_prime_C_prime (A_prime_B_prime_C_prime_out, Da_qn, Db_qn, Dc_qn);
  and A_prime_BC (A_prime_BC_out, Da_qn, Db_q, Dc_q);
  and BC_prime (BC_prime_out, Db_q, Dc_qn);
  and A_prime_B_prime_C_prime_2 (A_prime_B_prime_C_prime_2_out, Da_qn, Db_qn, Dc_qn);
  and A_prime_B (A_prime_B_out, Da_qn, Db_q);
  Clock clock_1 (.out(clock_1_out));
  or or_1 (or_1_out, A_prime_B_prime_C_prime_out, A_prime_BC_out);
  or or_2 (or_2_out, BC_prime_out, A_prime_B_prime_C_prime_2_out);
  LED led_1 (.in(Da_q));
  D_Flip_Flop Da (.clk(clock_1_out), .D(or_1_out), .Q(Da_q), .Qn(Da_qn));  // open: preset, en, reset
  D_Flip_Flop Db (.clk(clock_1_out), .D(or_2_out), .Q(Db_q), .Qn(Db_qn));  // open: preset, en, reset
  D_Flip_Flop Dc (.clk(clock_1_out), .D(A_prime_B_out), .Q(Dc_q), .Qn(Dc_qn));  // open: preset, en, reset
  LED led_2 (.in(Db_q));
  LED led_3 (.in(Dc_q));

  // Notes on the sheet:
  //   A'
  //   B'
  //   C'
  //   B
  //   C
endmodule
