// Logisim project Lab 13b.circ as structural Verilog: 1 circuit, main circuit main
module main (
  input  X
);

  wire A_prime_B_prime_C_prime_X_out, A_prime_BC_out, A_prime_BCX_out, A_prime_BX_out, A_prime_BX_prime_out,
       A_prime_C_prime_X_out, AB_prime_CX_prime_2_out, AB_prime_CX_prime_out, ABC_prime_X_prime_out,
       BC_prime_out, clock_1_out, Da_q, Da_qn, Db_q, Db_qn, Dc_q, Dc_qn, or_1_out, or_2_out, or_3_out,
       X_prime_out;

  not X_prime (X_prime_out, X);
  and ABC_prime_X_prime (ABC_prime_X_prime_out, Da_q, Db_q, Dc_qn, X_prime_out);
  and AB_prime_CX_prime (AB_prime_CX_prime_out, Da_q, Db_qn, Dc_q, X_prime_out);
  and A_prime_BCX (A_prime_BCX_out, Da_qn, Db_q, Dc_q, X);
  and A_prime_B_prime_C_prime_X (A_prime_B_prime_C_prime_X_out, Da_qn, Db_qn, Dc_qn, X);
  and BC_prime (BC_prime_out, Db_q, Dc_qn);
  and A_prime_BX_prime (A_prime_BX_prime_out, Da_qn, Db_q, X_prime_out);
  and A_prime_C_prime_X (A_prime_C_prime_X_out, Da_qn, Dc_qn, X);
  and A_prime_BX (A_prime_BX_out, Da_qn, Db_q, X);
  and A_prime_BC (A_prime_BC_out, Da_qn, Db_q, Dc_q);
  and AB_prime_CX_prime_2 (AB_prime_CX_prime_2_out, Da_q, Db_qn, Dc_q, X_prime_out);
  Clock clock_1 (.out(clock_1_out));
  or or_1 (or_1_out, ABC_prime_X_prime_out, AB_prime_CX_prime_out, A_prime_BCX_out, A_prime_B_prime_C_prime_X_out);
  or or_2 (or_2_out, BC_prime_out, A_prime_BX_prime_out, A_prime_C_prime_X_out);
  or or_3 (or_3_out, A_prime_BX_out, A_prime_BC_out, AB_prime_CX_prime_2_out);
  D_Flip_Flop Da (.clk(clock_1_out), .D(or_1_out), .Q(Da_q), .Qn(Da_qn));  // open: preset, en, reset
  D_Flip_Flop Db (.clk(clock_1_out), .D(or_2_out), .Q(Db_q), .Qn(Db_qn));  // open: preset, en, reset
  D_Flip_Flop Dc (.clk(clock_1_out), .D(or_3_out), .Q(Dc_q), .Qn(Dc_qn));  // open: preset, en, reset
  LED led_1 (.in(Db_q));
  LED led_2 (.in(Da_q));
  LED led_3 (.in(Dc_q));

  // Notes on the sheet:
  //   Input
  //   Clock
  //   Output
endmodule
