// Logisim project Lab 14a.circ as structural Verilog: 1 circuit, main circuit main
module main (
  input  X
);

  wire A_prime_B_prime_C_prime_X_2_out, A_prime_B_prime_C_prime_X_out, A_prime_BC_prime_X_out,
       A_prime_BCX_2_out, A_prime_BCX_out, AB_prime_CX_2_out, AB_prime_CX_out, ABC_prime_X_out, Clock_out,
       or_1_out, or_2_out, or_3_out, Ta_q, Ta_qn, Tb_q, Tb_qn, Tc_q, Tc_qn;

  and ABC_prime_X (ABC_prime_X_out, Ta_q, Tb_q, Tc_qn, X);
  and AB_prime_CX (AB_prime_CX_out, Ta_q, Tb_qn, Tc_q, X);
  and A_prime_BCX (A_prime_BCX_out, Ta_qn, Tb_q, Tc_q, X);
  and A_prime_B_prime_C_prime_X (A_prime_B_prime_C_prime_X_out, Ta_qn, Tb_qn, Tc_qn, X);
  and A_prime_BCX_2 (A_prime_BCX_2_out, Ta_qn, Tb_q, Tc_q, X);
  and A_prime_B_prime_C_prime_X_2 (A_prime_B_prime_C_prime_X_2_out, Ta_qn, Tb_qn, Tc_qn, X);
  and A_prime_BC_prime_X (A_prime_BC_prime_X_out, Ta_qn, Tb_q, Tc_qn, X);
  and AB_prime_CX_2 (AB_prime_CX_2_out, Ta_q, Tb_qn, Tc_q, X);
  or or_1 (or_1_out, ABC_prime_X_out, AB_prime_CX_out, A_prime_BCX_out, A_prime_B_prime_C_prime_X_out);
  or or_2 (or_2_out, A_prime_BCX_2_out, A_prime_B_prime_C_prime_X_2_out);
  or or_3 (or_3_out, A_prime_BC_prime_X_out, AB_prime_CX_2_out);
  Clock Clock (.out(Clock_out));
  LED led_1 (.in(Ta_q));
  T_Flip_Flop Ta (.clk(Clock_out), .T(or_1_out), .Q(Ta_q), .Qn(Ta_qn));  // open: preset, reset, en
  T_Flip_Flop Tb (.clk(Clock_out), .T(or_2_out), .Q(Tb_q), .Qn(Tb_qn));  // open: preset, reset, en
  T_Flip_Flop Tc (.clk(Clock_out), .T(or_3_out), .Q(Tc_q), .Qn(Tc_qn));  // open: preset, reset, en
  LED led_2 (.in(Tb_q));
  LED led_3 (.in(Tc_q));

  // Notes on the sheet:
  //   Input
  //   Output
endmodule
