// Logisim project Lab 14a2.circ as structural Verilog: 1 circuit, main circuit main
module main (
);

  wire A_prime_B_prime_CD_out, A_prime_BCD_2_out, A_prime_BCD_out, A_prime_C_prime_D_out, A_prime_CD_out,
       A_prime_D_out, A_prime_D_prime_out, A_q, A_qn, AB_prime_C_prime_D_out, B_prime_C_prime_D_out,
       B_prime_C_prime_D_prime_out, B_q, B_qn, C_q, C_qn, clock_1_out, D_q, D_qn, or_1_out, or_2_out;

  and A_prime_BCD (A_prime_BCD_out, A_qn, B_q, C_q, D_q);
  and AB_prime_C_prime_D (AB_prime_C_prime_D_out, A_q, B_qn, C_qn, D_q);
  and A_prime_B_prime_CD (A_prime_B_prime_CD_out, A_qn, B_qn, C_q, D_q);
  and A_prime_BCD_2 (A_prime_BCD_2_out, A_qn, B_q, C_q, D_q);
  and A_prime_C_prime_D (A_prime_C_prime_D_out, A_qn, C_qn, D_q);
  and A_prime_CD (A_prime_CD_out, A_qn, C_q, D_q);
  and A_prime_D_prime (A_prime_D_prime_out, A_qn, D_qn);
  and B_prime_C_prime_D_prime (B_prime_C_prime_D_prime_out, B_qn, C_qn, D_qn);
  and A_prime_D (A_prime_D_out, A_qn, D_q);
  and B_prime_C_prime_D (B_prime_C_prime_D_out, B_qn, C_qn, D_q);
  or or_1 (or_1_out, A_prime_D_prime_out, B_prime_C_prime_D_prime_out);
  or or_2 (or_2_out, A_prime_D_out, B_prime_C_prime_D_out);
  Clock clock_1 (.out(clock_1_out));
  J_K_Flip_Flop A (
    .J(A_prime_BCD_out), .clk(clock_1_out), .K(AB_prime_C_prime_D_out), .Q(A_q), .Qn(A_qn));  // open: preset, en, reset
  J_K_Flip_Flop B (
    .J(A_prime_B_prime_CD_out), .clk(clock_1_out), .K(A_prime_BCD_2_out), .Q(B_q), .Qn(B_qn));  // open: preset, en, reset
  J_K_Flip_Flop C (
    .J(A_prime_C_prime_D_out), .clk(clock_1_out), .K(A_prime_CD_out), .Q(C_q), .Qn(C_qn));  // open: preset, en, reset
  J_K_Flip_Flop D (.J(or_1_out), .clk(clock_1_out), .K(or_2_out), .Q(D_q), .Qn(D_qn));  // open: preset, en, reset
  LED led_1 (.in(A_q));
  LED led_2 (.in(B_q));
  LED led_3 (.in(D_q));
  LED led_4 (.in(C_q));
endmodule
