// Logisim project Lab 14b.circ as structural Verilog: 1 circuit, main circuit main
module main (
  input  in_1,
  input  in_2
);

  wire and_1_out, and_2_out, clock_1_out, not_2_out, or_1_out, t_ff_1_q, t_ff_2_q, t_ff_2_qn;

  // NOT_Gate not_1 has open pins: in=in_1, out=open
  not not_2 (not_2_out, in_2);
  and and_1 (and_1_out, in_1, not_2_out, t_ff_2_qn);
  and and_2 (and_2_out, in_1, in_2, t_ff_2_q);
  or or_1 (or_1_out, and_1_out, and_2_out);
  Clock clock_1 (.out(clock_1_out));
  T_Flip_Flop t_ff_1 (.clk(clock_1_out), .T(or_1_out), .Q(t_ff_1_q));  // open: Qn, preset, reset, en
  T_Flip_Flop t_ff_2 (.clk(clock_1_out), .T(in_1), .Q(t_ff_2_q), .Qn(t_ff_2_qn));  // open: preset, reset, en
  LED led_1 (.in(t_ff_2_q));
  LED led_2 (.in(t_ff_1_q));
endmodule
