// Logisim project Lab 15a.circ as structural Verilog: 1 circuit, main circuit main
module main (
  input  X,
  input  Y
);

  wire ABC_out, clock_1_out, d_ff_1_q, d_ff_2_q, d_ff_3_q, or_1_out, or_2_out, X_prime_B_out, X_prime_out,
       X_prime_Y_out, XA_out, XC_out, YB_out;

  not X_prime (X_prime_out, X);
  and X_prime_Y (X_prime_Y_out, X_prime_out, Y);
  and XA (XA_out, X, d_ff_1_q);
  and X_prime_B (X_prime_B_out, X_prime_out, d_ff_2_q);
  and XC (XC_out, X, d_ff_3_q);
  and YB (YB_out, Y, d_ff_2_q);
  and ABC (ABC_out, d_ff_1_q, d_ff_2_q, d_ff_3_q);
  or or_1 (or_1_out, X_prime_Y_out, XA_out);
  or or_2 (or_2_out, X_prime_B_out, XC_out);
  Clock clock_1 (.out(clock_1_out));
  LED led_1 (.in(d_ff_1_q));
  D_Flip_Flop d_ff_1 (.clk(clock_1_out), .D(or_1_out), .Q(d_ff_1_q));  // open: Qn, preset, en, reset
  D_Flip_Flop d_ff_2 (.clk(clock_1_out), .D(or_2_out), .Q(d_ff_2_q));  // open: Qn, preset, en, reset
  D_Flip_Flop d_ff_3 (.clk(clock_1_out), .D(YB_out), .Q(d_ff_3_q));  // open: Qn, preset, en, reset
  LED led_2 (.in(d_ff_3_q));
  LED led_3 (.in(d_ff_2_q));
  LED led_4 (.in(ABC_out));
endmodule
