// Logisim project Lab 15b.circ as structural Verilog: 1 circuit, main circuit main
module main (
  input  X
);

  wire AB_out, AB_prime_out, clock_1_out, or_1_out, or_2_out, Ta_q, Ta_qn, Tb_q, Tb_qn, XA_prime_out,
       XB_prime_out;

  and XA_prime (XA_prime_out, X, Ta_qn);
  and AB_prime (AB_prime_out, Ta_q, Tb_qn);
  and XB_prime (XB_prime_out, X, Tb_qn);
  and AB (AB_out, Ta_q, Tb_q);
  Clock clock_1 (.out(clock_1_out));
  or or_1 (or_1_out, XA_prime_out, AB_prime_out);
  or or_2 (or_2_out, XB_prime_out, AB_out);
  T_Flip_Flop Ta (.clk(clock_1_out), .T(or_1_out), .Q(Ta_q), .Qn(Ta_qn));  // open: preset, reset, en
  T_Flip_Flop Tb (.clk(clock_1_out), .T(or_2_out), .Q(Tb_q), .Qn(Tb_qn));  // open: preset, reset, en
  LED led_1 (.in(Ta_q));
  LED led_2 (.in(Tb_q));
endmodule
