// Logisim project Lab10b.circ as structural Verilog: 1 circuit, main circuit main
module main (
  input  X,
  input  Y,
  input  Z,
  input  W
);

  wire and_1_out, and_2_out, and_3_out, and_4_out, and_5_out, or_1_out, or_2_out, or_3_out, or_4_out,
       W_prime_out, X_prime_out, X_prime_Y_prime_ZW_out, X_prime_YZ_prime_out, X_prime_Z_prime_W_out,
       X_prime_ZW_prime_out, XYZ_out, XZ_prime_W_prime_out, XZW_out, Y_prime_out, YZ_prime_W_out,
       YZW_prime_out, Z_prime_out, Z_prime_W_prime_out, ZW_prime_out;

  not X_prime (X_prime_out, X);
  not Y_prime (Y_prime_out, Y);
  not Z_prime (Z_prime_out, Z);
  not W_prime (W_prime_out, W);
  and and_1 (and_1_out, X, Y);
  and and_2 (and_2_out, X, W);
  and and_3 (and_3_out, X, Z);
  and and_4 (and_4_out, Y, Z, W);
  and and_5 (and_5_out, X, Y_prime_out, Z_prime_out, W_prime_out);
  and X_prime_Y_prime_ZW (X_prime_Y_prime_ZW_out, X_prime_out, Y_prime_out, Z, W);
  and YZ_prime_W (YZ_prime_W_out, Y, Z_prime_out, W);
  and YZW_prime (YZW_prime_out, Y, Z, W_prime_out);
  and X_prime_YZ_prime (X_prime_YZ_prime_out, X_prime_out, Y, Z_prime_out);
  and XYZ (XYZ_out, X, Y, Z);
  and XZ_prime_W_prime (XZ_prime_W_prime_out, X, Z_prime_out, W_prime_out);
  and X_prime_Z_prime_W (X_prime_Z_prime_W_out, X_prime_out, Z_prime_out, W);
  and XZW (XZW_out, X, Z, W);
  and X_prime_ZW_prime (X_prime_ZW_prime_out, X_prime_out, Z, W_prime_out);
  and Z_prime_W_prime (Z_prime_W_prime_out, Z_prime_out, W_prime_out);
  and ZW_prime (ZW_prime_out, Z, W_prime_out);
  or or_1 (or_1_out, and_1_out, and_2_out, and_3_out, and_4_out);
  or or_2 (or_2_out, XZ_prime_W_prime_out, X_prime_Z_prime_W_out, XZW_out, X_prime_ZW_prime_out);
  or or_3 (or_3_out, Z_prime_W_prime_out, ZW_prime_out);
  LED A (.in(or_1_out));
  LED B (.in(or_4_out));
  or or_4 (or_4_out, and_5_out, X_prime_Y_prime_ZW_out, YZ_prime_W_out, YZW_prime_out, X_prime_YZ_prime_out, XYZ_out);
  LED C (.in(or_2_out));
  LED D (.in(or_3_out));

  // Notes on the sheet:
  //   XY
  //   XW
  //   XZ
  //   YZW
  //   XY'Z'W'
endmodule
