// Logisim project Lab8b.circ as structural Verilog: 1 circuit, main circuit main
module main (
  input  A,
  input  B,
  input  C,
  input  D
);

  wire A_prime_out, AND1_2_out, AND1_out, AND2_2_out, AND2_out, AND3_2_out, AND3_out, AND4_2_out, AND4_out,
       AND5_out, AND6_out, AND7_out, AND8_out, AND9_out, AND_out, B_prime_out, C_prime_out, D_prime_out,
       OR1_out, OR2_out, OR3_out, OR4_out, OR5_out, OR6_out, OR7_out;

  not A_prime (A_prime_out, A);
  not B_prime (B_prime_out, B);
  not C_prime (C_prime_out, C);
  not D_prime (D_prime_out, D);
  and AND1 (AND1_out, A, C_prime_out);
  and AND2 (AND2_out, B_prime_out, D);
  and AND3 (AND3_out, A_prime_out, C, D);
  and AND4 (AND4_out, A, B, C, D);
  and AND1_2 (AND1_2_out, A_prime_out, B_prime_out, C_prime_out, D);
  and AND2_2 (AND2_2_out, A_prime_out, B_prime_out, C, D);
  and AND3_2 (AND3_2_out, A_prime_out, B, C, D);
  and AND4_2 (AND4_2_out, A, B_prime_out, C_prime_out, D_prime_out);
  and AND5 (AND5_out, A, B_prime_out, C_prime_out, D);
  and AND6 (AND6_out, A, B_prime_out, C, D);
  and AND7 (AND7_out, A, B, C_prime_out, D_prime_out);
  and AND8 (AND8_out, A, B, C_prime_out, D);
  and AND9 (AND9_out, A, B, C, D);
  or OR1 (OR1_out, A, B, C, D);
  or OR2 (OR2_out, A, B, C_prime_out, D);
  or OR3 (OR3_out, A, B_prime_out, C, D);
  or OR4 (OR4_out, A, B_prime_out, C, D_prime_out);
  or OR5 (OR5_out, A, B_prime_out, C_prime_out, D);
  or OR6 (OR6_out, A_prime_out, B, C_prime_out, D);
  or OR7 (OR7_out, A_prime_out, B_prime_out, C_prime_out, D);
  and AND (AND_out, OR1_out, OR2_out, OR3_out, OR4_out, OR5_out, OR6_out, OR7_out);
  or OR (AND_out, AND1_out, AND2_out, AND3_out, AND4_out);
  or OR_2 (AND_out, AND1_2_out, AND2_2_out, AND3_2_out, AND4_2_out, AND5_out, AND6_out, AND7_out, AND8_out, AND9_out);
  LED led_1 (.in(AND_out));
endmodule
