// Logisim project Lab8b1.circ as structural Verilog: 1 circuit, main circuit main
// AND1
module main (
  input  X,
  input  Y,
  input  Z
);

  wire AND1_2_out, AND1_out, AND2_2_out, AND2_out, AND3_2_out, AND3_out, AND4_out, AND5_out, OR1_out,
       OR2_out, OR3_out, OR_out, X_prime_out, Y_prime_out, Z_prime_out;

  not X_prime (X_prime_out, X);
  not Y_prime (Y_prime_out, Y);
  not Z_prime (Z_prime_out, Z);
  and AND1 (AND1_out, X_prime_out, Y_prime_out);
  and AND2 (AND2_out, Y, Z);
  and AND3 (AND3_out, X_prime_out, Y, Z_prime_out);
  and AND1_2 (AND1_2_out, X_prime_out, Y_prime_out, Z_prime_out);
  and AND2_2 (AND2_2_out, X_prime_out, Y_prime_out, Z);
  and AND3_2 (AND3_2_out, X_prime_out, Y, Z_prime_out);
  and AND4 (AND4_out, X_prime_out, Y, Z);
  and AND5 (AND5_out, X, Y, Z);
  or OR1 (OR1_out, X_prime_out, Y, Z);
  or OR2 (OR2_out, X_prime_out, Y, Z_prime_out);
  or OR3 (OR3_out, X_prime_out, Y_prime_out, Z);
  or OR (OR_out, AND1_out, AND2_out, AND3_out);
  or OR_2 (OR_out, AND1_2_out, AND2_2_out, AND3_2_out, AND4_out, AND5_out);
  and AND (OR_out, OR1_out, OR2_out, OR3_out);
  LED led_1 (.in(OR_out));
endmodule
