// Logisim project Lab9a.circ as structural Verilog: 1 circuit, main circuit main
module main (
  input  X,
  input  Y,
  input  Z
);

  wire AND1_out, AND2_out, AND3_out, OR1_out, OR2_out, OR3_out, OR_SOP_out;

  and AND1 (AND1_out, X, Y);
  and AND2 (AND2_out, X, Z);
  and AND3 (AND3_out, Y, Z);
  or OR1 (OR1_out, X, Y);
  or OR2 (OR2_out, X, Z);
  or OR3 (OR3_out, Y, Z);
  or OR_SOP (OR_SOP_out, AND1_out, AND2_out, AND3_out);
  and AND_POS (OR_SOP_out, OR1_out, OR2_out, OR3_out);
  LED led_1 (.in(OR_SOP_out));
endmodule
